# Fritzing sketch garage-door-controller (saved by Fritzing 0.9.4)
circuit board: 5.58094cm x 7.35506cm
breadboards: 1

parts:
  Q1 = NPN-Transistor [package="TO92 [THT]"]
  R3 = Resistor [tolerance=±5% resistance=1k package=THT]
  R4 = Resistor [tolerance=±5% resistance=10k package=THT]
  J3 = longpad pin header, 3 pins [form="long pad"]
  R2 = Resistor [tolerance=±5% resistance=10k package=THT]
  U1 = NodeMCU V1.0
  J1 = longpad pin header, 3 pins [form="long pad"]
  R1 = Resistor [tolerance=±5% resistance=10k package=THT]
  J2 = longpad pin header, 3 pins [form="long pad"]

nets:
  N1: Q1.E, J3.pin1, R2.Pin_1
  N2: Q1.B, R3.Pin_1
  N3: Q1.C, R4.Pin_1, U1.D2
  N4: R3.Pin_0, R4.Pin_0, U1.3V3, R1.Pin_0
  N5: J3.pin2, R2.Pin_0, U1.Vin
  N6: J3.pin3, U1.GND, J2.pin1
  N7: U1.D1, J1.pin2
  N8: U1.D5, J2.pin2
  N9: U1.D6, J2.pin3
  N10: U1.RST, J1.pin1, R1.Pin_1

custom parts:
  NodeMCU V1.0: ESP8266 based NodeMCU
